# Fritzing sketch mint-tin-permaproto (saved by Fritzing 0.9.5d)
breadboards: 1

parts:
  Part6 = TRRS 3.5mm Jack Breakout
  IC4 = IC, DIP package, 14 pins [chip_label="74AHCT14N -4"]
  Part7 = Adafruit Feather 32u4 Bluefruit [part_number="Adafruit #2829"]
  JACK2 = 2.1mm DC Barrel Jack
  Part8 = Adafruit MPM3610 5V

nets (from the breadboard view):
  GND: Part6.RING2, IC4.pin1, IC4.pin7, IC4.pin9, IC4.pin13, Part7.GND, JACK2.switch, Part8.GND
  N1: Part6.RING1, IC4.pin3
  N2: Part6.TIP, IC4.pin5
  N3: IC4.pin4, Part7.10
  N4: IC4.pin6, Part7.11
  N5: IC4.pin10, Part8.EN
  N6: IC4.pin11, JACK2.center, Part8.VIN
  N7: IC4.pin12, Part7.VBUS, Part8.5.0V
  N8: IC4.pin14, Part7.+3V3

notes:
  Red: 3V3
  Purple: 5V
  Orange: 12V
  Black: GND
  Black banded: GND/backside
  Green: HU
  Blue: Bike

custom parts:
  TRRS 3.5mm Jack Breakout: TRRS connectors are the audio-style connectors that you see on some phones, MP3 players and development boards. TRRS stands for “Tip, Ring, Ring, Sleeve,” which reflects the fact that, unlike a standard stereo connector, this actually has three conductors and a ground. Some devices use the extra conductor for a microphone (like hands-free headsets) or to carry a video signal (like in some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
  Adafruit Feather 32u4 Bluefruit: This is the Adafruit Feather 32u4 Bluefruit - our take on an 'all-in-one' Arduino-compatible + Bluetooth Low Energy with built in USB and battery charging. Its an Adafruit Feather 32u4 with a BTLE module, ready to rock! We have other boards in the Feather family, check'em out here. Bluetooth Low Energy is the hottest new low-power, 2.4GHz spectrum wireless protocol. In particular, its the only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
  2.1mm DC Barrel Jack: 2.1mm DC Barrel Jack with Thru-Hole Connectors (breadboardable)
